// Logisim project P3.circ as structural Verilog: 1 circuit, main circuit main
module main (
  output Overflow
);

  wire and_1_out, button_1_out, button_2_out, clock_1_out, clock_2_out, clock_3_out, clock_4_out,
       clock_5_out, clock_6_out, clock_7_out, clock_8_out, clock_9_out, clock_10_out, nor_1_out, xnor_1_out,
       xor_2_out;
  wire [3:0] C2_q_2, D3_q;
  wire [6:0] multiplexer_1_out;
  wire [7:0] A1_q, A2_q, A3_q, adder_1_out, adder_2_out, B3_q, bit_extender_1_out, bit_extender_2_out,
       bit_extender_3_out, C3_q, negator_1_out, PC_q, R1_q, rom_1_data, xor_1_out;
  wire [7:2] C2_q;

  Register PC (.D(adder_1_out), .en(1'b1), .clk(clock_1_out), .Q(PC_q), .clr(button_1_out));
  Clock clock_1 (.out(clock_1_out));
  Button button_1 (.out(button_1_out));
  ROM rom_1 (.addr(PC_q), .data(rom_1_data));
  Adder adder_1 (.a({8{1'b0}}), .b(PC_q), .out(adder_1_out), .cin(1'b1));  // open: cout
  Register A1 (.D(rom_1_data), .en(1'b1), .clk(clock_2_out), .Q(A1_q));  // open: clr
  Clock clock_2 (.out(clock_2_out));
  assign bit_extender_1_out = {{7{A1_q[1]}}, A1_q[1]};  // Bit_Extender bit_extender_1
  assign bit_extender_2_out = {{2{A1_q[7]}}, A1_q[7:2]};  // Bit_Extender bit_extender_2
  assign xor_1_out = bit_extender_1_out ^ bit_extender_2_out;  // XOR_Gate xor_1, 8 bits wide
  nor nor_1 (nor_1_out, A1_q[2], A1_q[3], A1_q[4], A1_q[5], A1_q[6], A1_q[7]);
  Register C2 (.D(A1_q), .en(1'b1), .clk(clock_3_out), .Q({C2_q, C2_q_2[1:0]}));  // open: clr
  Clock clock_3 (.out(clock_3_out));
  Register A2 (.D(xor_1_out), .en(1'b1), .clk(clock_4_out), .Q(A2_q));  // open: clr
  Clock clock_4 (.out(clock_4_out));
  D_Flip_Flop B2 (.D(and_1_out), .clk(clock_5_out), .Q(C2_q_2[2]));  // open: Qn, preset, reset
  and and_1 (and_1_out, nor_1_out, A1_q[0]);
  Clock clock_5 (.out(clock_5_out));
  xnor xnor_1 (xnor_1_out, A2_q[7], C2_q_2[3]);
  Adder adder_2 (.a({C2_q_2[3], multiplexer_1_out}), .b(A2_q), .out(adder_2_out), .cin(C2_q_2[1]));  // open: cout
  Register B3 (.D(bit_extender_3_out), .en(1'b1), .clk(clock_6_out), .Q(B3_q));  // open: clr
  assign bit_extender_3_out = {{1{C2_q[7]}}, {C2_q, C2_q_2[1]}};  // Bit_Extender bit_extender_3
  Clock clock_6 (.out(clock_6_out));
  Negator negator_1 (.in({C2_q_2[3], multiplexer_1_out}), .out(negator_1_out));
  and and_2 (Overflow, xnor_1_out, xor_2_out);
  xor xor_2 (xor_2_out, C2_q_2[3], adder_2_out[7]);
  Register A3 (.D(adder_2_out), .en(1'b1), .clk(clock_7_out), .Q(A3_q));  // open: clr
  Clock clock_7 (.out(clock_7_out));
  Register C3 (.D(negator_1_out), .en(1'b1), .clk(clock_8_out), .Q(C3_q));  // open: clr
  Clock clock_8 (.out(clock_8_out));
  Register #(.width(4)) D3 (.D(C2_q_2), .en(1'b1), .clk(clock_9_out), .Q(D3_q));  // open: clr
  Clock clock_9 (.out(clock_9_out));
  Register R1 (.D({C2_q_2[3], multiplexer_1_out}), .en(1'b1), .clk(clock_10_out), .Q(R1_q), .clr(button_2_out));
  Multiplexer #(.select(4), .width(8)) multiplexer_1 (
    .in0(B3_q), .in1(A3_q), .in2(B3_q), .in3(A3_q), .in5(R1_q), .in7(R1_q), .in8(B3_q), .in9(A3_q),
    .in10(B3_q), .in11(A3_q), .in13({8{1'b0}}), .in15(C3_q), .out({C2_q_2[3], multiplexer_1_out}), .sel(D3_q));  // open: in4, in6, in12, in14
  Clock clock_10 (.out(clock_10_out));
  Button button_2 (.out(button_2_out));
endmodule
